// Logisim project SAP-1.circ as structural Verilog
module ProgramCounter (
  input  Cp,
  input  nCLK,
  input  CLR,
  input  Ep,
  output [3:0] OUT_BUS
);

  wire adder_1_cout, adder_1_out, adder_2_cout, adder_2_out, adder_3_cout, adder_3_out, adder_4_out,
       not_1_out;
  wire [3:0] d_ff_1_q;

  not not_1 (not_1_out, nCLK);
  D_Flip_Flop d_ff_1 (.clk(not_1_out), .D(adder_1_out), .Q(d_ff_1_q[0]), .reset(CLR));  // open: Qn, preset, en
  Adder #(.width(1)) adder_1 (.a(Cp), .b(d_ff_1_q[0]), .out(adder_1_out), .cout(adder_1_cout));  // open: cin
  D_Flip_Flop d_ff_2 (.clk(not_1_out), .D(adder_2_out), .Q(d_ff_1_q[1]), .reset(CLR));  // open: Qn, preset, en
  D_Flip_Flop d_ff_3 (.clk(not_1_out), .D(adder_3_out), .Q(d_ff_1_q[2]), .reset(CLR));  // open: Qn, preset, en
  Adder #(.width(1)) adder_2 (.a(adder_1_cout), .b(d_ff_1_q[1]), .out(adder_2_out), .cout(adder_2_cout));  // open: cin
  D_Flip_Flop d_ff_4 (.clk(not_1_out), .D(adder_4_out), .Q(d_ff_1_q[3]), .reset(CLR));  // open: Qn, preset, en
  Adder #(.width(1)) adder_3 (.a(adder_2_cout), .b(d_ff_1_q[2]), .out(adder_3_out), .cout(adder_3_cout));  // open: cin
  assign OUT_BUS = Ep ? d_ff_1_q : 4'bz;  // Controlled_Buffer controlled_buffer_1
  Adder #(.width(1)) adder_4 (.a(adder_3_cout), .b(d_ff_1_q[3]), .out(adder_4_out));  // open: cin, cout
endmodule

module MemoryAddressRegister (
  input  CLK,
  input  [3:0] IN_BUS,
  input  nLm,
  input  CLR,
  output [3:0] OUT_RAM
);

  wire [3:0] controlled_buffer_1_out;

  assign controlled_buffer_1_out = nLm ? IN_BUS : 4'bz;  // Controlled_Buffer controlled_buffer_1
  D_Flip_Flop d_ff_1 (.clk(CLK), .D(controlled_buffer_1_out[0]), .Q(OUT_RAM[0]), .reset(CLR));  // open: Qn, preset, en
  D_Flip_Flop d_ff_2 (.clk(CLK), .D(controlled_buffer_1_out[1]), .Q(OUT_RAM[1]), .reset(CLR));  // open: Qn, preset, en
  D_Flip_Flop d_ff_3 (.clk(CLK), .D(controlled_buffer_1_out[2]), .Q(OUT_RAM[2]), .reset(CLR));  // open: Qn, preset, en
  D_Flip_Flop d_ff_4 (.clk(CLK), .D(controlled_buffer_1_out[3]), .Q(OUT_RAM[3]), .reset(CLR));  // open: Qn, preset, en
endmodule
